// Logisim project Excess3_Adder.circ as structural Verilog: 1 circuit, main circuit Excess3_Adder
module Excess3_Adder (
  input  [3:0] A,
  input  [3:0] B,
  output [3:0] Sum,
  output C_out
);

  wire [3:0] adder_1_out, undriven;

  Adder #(.width(4)) adder_1 (.a(A), .b(B), .out(adder_1_out), .cin(1'b0), .cout(C_out));
  not not_1 (undriven[2], C_out);
  Adder #(.width(4)) adder_2 (
    .a(adder_1_out), .b({undriven[3:2], undriven[2], undriven[0]}), .out(Sum), .cin(1'b0));  // open: cout

  // Notes on the sheet:
  //   Excess-3 Adder
  //   Designed by: Vansh Patel (25bce190)
endmodule
